# Fritzing sketch homPhone回路図全体 (saved by Fritzing 0.9.3b)
breadboards: 1

parts:
  SP1 = SPEAKER [package=pcb_mount_speaker]
  Raspberry_Pi_Zero_W = Raspberry Pi Zero
  S1 = Round Pushbutton
  LED2 = smd LED [color="Yellow (585nm)" package="1206 [SMD]"]
  AE-MOD1 = AE-LXDC55-5V-Down
  JP3 = USB_MICROB_PLUG [package=micro-b-th]
  Power_plug4 = Power plug
  LED3 = smd LED [color="Green (555nm)" package="1206 [SMD]"]
  マイク = Breakout Board for Electret Microphone
  U2 = Mono 2.6W Class D Amplifier [package=8-tdfn-ep]
  JP7 = RCA [package=rca]
  JP8 = RCA [package=rca]
  R1 = Resistor [tolerance=±5% resistance=10k package=THT]
  R2 = Resistor [tolerance=±5% resistance=75 package=THT]
  R3 = Resistor [tolerance=±5% resistance=75 package=THT]

nets:
  N1: SP1.+, U2.OUT-
  N2: SP1.-, U2.OUT+
  N3: Raspberry_Pi_Zero_W.GPIO21, S1.leg1
  N4: Raspberry_Pi_Zero_W.GPIO20, LED2.anode
  N5: Raspberry_Pi_Zero_W.GPIO16, LED3.anode
  GND: Raspberry_Pi_Zero_W.GND, AE-MOD1.GND, JP3.GND, Power_plug4.GND, U2.GND, R1.Pin_0, R2.Pin_0, R3.Pin_0
  N6: S1.leg0, R1.Pin_1
  N7: LED2.cathode, R3.Pin_1
  9V: AE-MOD1.IN, Power_plug4.VCC
  5V: AE-MOD1.OUT, JP3.VCC, U2.VDD
  N8: LED3.cathode, R2.Pin_1
  N9: マイク.VCC, マイク.AUD, JP8.PIN
  N10: マイク.GND, JP8.SHELL
  N11: U2.IN+, JP7.PIN
  N12: U2.IN-, JP7.SHELL

custom parts:
  AE-LXDC55-5V-Down: AE-LXDC55-5V upside down
