# Fritzing sketch pi用シールド回路図 (saved by Fritzing 0.9.3b)
perfboards: 1

parts:
  パーツ4 = FTDI Basic Programmer
  J3 = double row male pin header, 20 pins [form="♂ (male)"]
  J4 = double row male pin header, 20 pins [form="♂ (male)"]
  JP1 = molex 70553 2P [part_number=70553-0002 form="♀ (female)" package="90 degree"]
  JP2 = molex 70553 2P [part_number=70553-0002 form="♀ (female)" package="90 degree"]
  JP3 = molex 70553 2P [part_number=70553-0002 form="♀ (female)" package="90 degree"]
  S3 = Square Pushbutton
  LED1 = smd LED [color="Yellow (585nm)" package="0603 [SMD]"]
  LED2 = smd LED [color="Green (560nm)" package="0603 [SMD]"]
  R1 = Resistor [tolerance=±5% resistance=75 package=THT]
  R2 = Resistor [tolerance=±5% resistance=75 package=THT]
  R3 = Resistor [tolerance=±5% resistance=10k package=THT]
  J5 = female pin header, 2 pins [form="♀ (female)"]
  J6 = female pin header, 2 pins [form="♀ (female)"]
  J7 = female pin header, 2 pins [form="♀ (female)"]
  Raspberry_Pi_Zero1 = Raspberry Pi Zero  # not connected

nets:
  N1: パーツ4.RXI, J4.pin4
  N2: パーツ4.TXO, J4.pin5
  N3: パーツ4.GND, J4.pin3
  N4: J3.pin9, JP1.1
  N5: J3.pin13, JP2.2, JP3.2
  N6: J3.pin20, R3.Pin_0
  N7: J4.pin18, R1.Pin_1
  N8: J4.pin19, R2.Pin_1
  N9: J4.pin20, JP1.2, R3.Pin_1
  N10: JP2.1, R1.Pin_0
  N11: JP3.1, R2.Pin_0
  N12: S3.leg0, J5.pin1
  N13: S3.leg1, J5.pin2
  N14: LED1.cathode, J6.pin2
  N15: LED1.anode, J6.pin1
  N16: LED2.cathode, J7.pin2
  N17: LED2.anode, J7.pin1

custom parts:
  molex 70553 2P: Header
